# Fritzing sketch fz-charduindi (saved by Fritzing 0.9.3b)
circuit board: 14.5058cm x 6.7205cm
breadboards: 1

parts:
  LED13 = LED - 5mm [color="Green (555nm)" part_number=C503B-GCN-CY0C0791 current=20mA package="5 mm [THT]"]
  LED6 = LED - 5mm [color="Green (555nm)" part_number=C503B-GCN-CY0C0791 current=20mA package="5 mm [THT]"]
  LED11 = LED - 5mm [color="Green (555nm)" part_number=C503B-GCN-CY0C0791 current=20mA package="5 mm [THT]"]
  R5 = Resistor [tolerance=±5% resistance=75 package=THT]
  LED12 = LED - 5mm [color="Green (555nm)" part_number=C503B-GCN-CY0C0791 current=20mA package="5 mm [THT]"]
  LED15 = LED - 5mm [color="Green (555nm)" part_number=C503B-GCN-CY0C0791 current=20mA package="5 mm [THT]"]
  LED14 = LED - 5mm [color="Green (555nm)" part_number=C503B-GCN-CY0C0791 current=20mA package="5 mm [THT]"]
  R3 = Resistor [tolerance=±5% resistance=75 package=THT]
  LED2 = LED - 5mm [color="Green (555nm)" part_number=C503B-GCN-CY0C0791 current=20mA package="5 mm [THT]"]
  ATMEGA328p = atmega328 [package=dip]
  LED8 = LED - 5mm [color="Green (555nm)" part_number=C503B-GCN-CY0C0791 current=20mA package="5 mm [THT]"]
  LED9 = LED - 5mm [color="Green (555nm)" part_number=C503B-GCN-CY0C0791 current=20mA package="5 mm [THT]"]
  16Mhz = CRYSTAL - kHz [frequency="16 MHz"]
  LED7 = LED - 5mm [color="Green (555nm)" part_number=C503B-GCN-CY0C0791 current=20mA package="5 mm [THT]"]
  LED18 = LED - 5mm [color="Green (555nm)" part_number=C503B-GCN-CY0C0791 current=20mA package="5 mm [THT]"]
  C3 = Ceramic Capacitor [package="200 mil [THT, multilayer]"]
  R4 = Resistor [tolerance=±5% resistance=75 package=THT]
  C2 = Ceramic Capacitor [package="200 mil [THT, multilayer]"]
  LED16 = LED - 5mm [color="Green (555nm)" part_number=C503B-GCN-CY0C0791 current=20mA package="5 mm [THT]"]
  R1 = Resistor [tolerance=±5% resistance=75 package=THT]
  TTL = USB TTL Serial Cable
  LED17 = LED - 5mm [color="Green (555nm)" part_number=C503B-GCN-CY0C0791 current=20mA package="5 mm [THT]"]
  LED20 = LED - 5mm [color="Green (555nm)" part_number=C503B-GCN-CY0C0791 current=20mA package="5 mm [THT]"]
  LED5 = LED - 5mm [color="Green (555nm)" part_number=C503B-GCN-CY0C0791 current=20mA package="5 mm [THT]"]
  LED4 = LED - 5mm [color="Green (555nm)" part_number=C503B-GCN-CY0C0791 current=20mA package="5 mm [THT]"]
  LED10 = LED - 5mm [color="Green (555nm)" part_number=C503B-GCN-CY0C0791 current=20mA package="5 mm [THT]"]
  LED3 = LED - 5mm [color="Green (555nm)" part_number=C503B-GCN-CY0C0791 current=20mA package="5 mm [THT]"]
  LED1 = LED - 5mm [color="Green (555nm)" part_number=C503B-GCN-CY0C0791 current=20mA package="5 mm [THT]"]
  LED19 = LED - 5mm [color="Green (555nm)" part_number=C503B-GCN-CY0C0791 current=20mA package="5 mm [THT]"]
  R2 = Resistor [tolerance=±5% resistance=75 package=THT]

nets:
  N1: LED13.cathode, LED15.cathode, LED14.cathode, R4.Pin_0, LED16.cathode
  charlie 5: LED13.anode, LED9.anode, R1.Pin_1, LED17.anode, LED5.anode
  N2: LED6.cathode, LED8.cathode, LED7.cathode, LED5.cathode, R2.Pin_0
  charlie 3: LED6.anode, LED15.anode, R3.Pin_1, LED2.anode, ATMEGA328p.D4, LED20.anode
  N3: LED11.cathode, LED12.cathode, R3.Pin_0, LED9.cathode, LED10.cathode
  charlie 2: LED11.anode, ATMEGA328p.D3_(PWM), LED7.anode, R4.Pin_1, LED3.anode, LED19.anode
  N4: R5.Pin_0, LED18.cathode, LED17.cathode, LED20.cathode, LED19.cathode
  charlie 1: R5.Pin_1, LED12.anode, ATMEGA328p.D2, LED8.anode, LED16.anode, LED4.anode
  charlie 4: LED14.anode, ATMEGA328p.D5_(PWM), LED18.anode, LED10.anode, LED1.anode, R2.Pin_1
  N5: LED2.cathode, R1.Pin_0, LED4.cathode, LED3.cathode, LED1.cathode
  rx: ATMEGA328p.D0_(RX), TTL.TX
  tx: ATMEGA328p.D1_(TX), TTL.RX
  5vcc: ATMEGA328p.VCC, TTL.5V
  GND: ATMEGA328p.GND, C3.0, C2.0, TTL.GND
  xtal1: ATMEGA328p.XLAT1, 16Mhz.pin_1, C2.1
  xtal2: ATMEGA328p.XLAT2, 16Mhz.pin_0, C3.1

custom parts:
  Ceramic Capacitor: 22 pF multilayer Ceramic Capacitor
